# Fritzing sketch Domotic Control House (saved by Fritzing 0.9.3b)
breadboards: 2

parts:
  U1 = ESP32-30Pin [part_number=ESP32-30Pin]
  Componente1 = MQ-4
  Water_Level_Sensor1 = Water Level Sensor
  J1 = Basic Servo
  J2 = Basic Servo
  S2 = Pushbutton [package="[THT]"]
  DHT11_1 = DHT11 module
  e-radionica_com1 = LM393 LDR breakout [part_number=100027]
  KY-1 = Keyes Relay [package=THT]
  KY-2 = Keyes Relay [package=THT]
  Mod1 = KY-025 Reed Switch Module [package="Breakout board"]
  LED1 = LEDs [package=led10mm]
  Power_plug1 = Power plug
  F1 = Fan - Ventilador [package=THT]
  Part3 = Lilypad Battery Connect
  J3 = Piezo Speaker

nets:
  VCC: U1.VIN, J1.vcc, J2.vcc, KY-1.power, KY-2.power
  GND: U1.GND, Componente1.GND, Water_Level_Sensor1.GND, J1.gnd, J2.gnd, e-radionica_com1.GND, J3.pin1
  N1: U1.D13, J1.pulse
  N2: U1.D12, J2.pulse
  N3: U1.D27, S2.Pin_3, S2.Pin_4, J3.pin2
  N4: U1.D34, Water_Level_Sensor1.SIG
  N5: U1.VN, Componente1.AO
  N6: U1.VP, e-radionica_com1.AO
  VCC_2: Componente1.VCC, Water_Level_Sensor1.VCC, S2.Pin_1, S2.Pin_2, DHT11_1.VCC, e-radionica_com1.VCC, Mod1.+
  N7: DHT11_1.GND, KY-1.ground, KY-2.ground, Mod1.G
  N8: KY-1.NC, Part3.-
  N9: KY-1.C, LED1.C
  N10: KY-2.NC, Power_plug1.GND
  N11: KY-2.C, F1.GND
  N12: LED1.A, Part3.+
  VCC_3: Power_plug1.VCC, F1.5V

custom parts:
  ESP32-30Pin: Generic 30-Pin ESP32
  Water Level Sensor: A water level sensor. This sensor operates at 3V to 5V. The Sig (signal) pin outputs an analogue signal that is in proportion to the amount of water in contact with the sensor.
  DHT11 module: DHT11 black pcb module
  Keyes Relay: The Keyes 5V relay module is suitable for SCM development, home appliance control. It uses a 5V~12V TIL control signal which can control DC / AC signal.
  KY-025 Reed Switch Module: KY-025 Reed Switch Module, it reacts in the presence of a magnetic field.
  LEDs: LEDs Standard schematic elements and footprints for 5mm, 3mm, 1206, and 0603 sized LEDs. 5mm - Spark Fun Electronics SKU : COM-00529 (and others)
  Fan - Ventilador: Ventilador de 2 pines, se encuentra comunmente en computadoras de escritorio
